# Fritzing sketch WatctowerHAT (saved by Fritzing 0.9.3b)

parts:
  proto2 = Adafruit_PermaProto_1_4_Board
  Part6 = Adafruit Perma-Proto HAT [part_number="Adafruit #2314 and #2310"]
  R27 = PHOTOCELL [package=photocell]
  R30 = Resistor [tolerance=±5% resistance=330 package="2512 [SMD]"]
  R31 = Resistor [tolerance=±5% resistance=330 package="2512 [SMD]"]
  LED22 = smd LED [color="Red (633nm)" package="0603 [SMD]"]
  J7 = Basic Servo
  R33 = Resistor [tolerance=±5% resistance=10k package="2512 [SMD]"]
  LED23 = smd LED [color="Infrared (850nm)" package="1206 [SMD]"]  # not connected
  LED24 = smd LED [color="Infrared (850nm)" package="1206 [SMD]"]  # not connected
  LED25 = smd LED [color="Infrared (850nm)" package="1206 [SMD]"]  # not connected
  LED26 = smd LED [color="Infrared (850nm)" package="1206 [SMD]"]  # not connected
  LED27 = smd LED [color="Infrared (850nm)" package="1206 [SMD]"]  # not connected
  LED28 = smd LED [color="Infrared (850nm)" package="1206 [SMD]"]  # not connected
  LED29 = smd LED [color="Infrared (850nm)" package="1206 [SMD]"]  # not connected
  LED30 = smd LED [color="Infrared (850nm)" package="1206 [SMD]"]  # not connected
  LED31 = smd LED [color="Infrared (850nm)" package="1206 [SMD]"]  # not connected
  R34 = Resistor [tolerance=±5% resistance=27 package="2512 [SMD]"]  # not connected
  R35 = Resistor [tolerance=±5% resistance=27 package="2512 [SMD]"]  # not connected
  LED32 = smd LED [color="Infrared (850nm)" package="1206 [SMD]"]  # not connected
  R36 = Resistor [tolerance=±5% resistance=27 package="2512 [SMD]"]  # not connected
  R37 = Resistor [tolerance=±5% resistance=27 package="2512 [SMD]"]  # not connected
  LED33 = smd LED [color="Infrared (850nm)" package="1206 [SMD]"]  # not connected
  LED34 = smd LED [color="Infrared (850nm)" package="1206 [SMD]"]  # not connected
  R38 = Resistor [tolerance=±5% resistance=150 package="2512 [SMD]"]  # not connected
  LED35 = smd LED [color="Infrared (850nm)" package="1206 [SMD]"]  # not connected
  R39 = Resistor [tolerance=±5% resistance=150 package="2512 [SMD]"]  # not connected
  LED36 = smd LED [color="Infrared (850nm)" package="1206 [SMD]"]  # not connected
  Q4 = NPN-Transistor [package="TO92 [THT]"]
  U1 = ATTiny84 [package=dip]
  J9 = female pin header, 2 pins [form="♀ (female)"]
  F1 = Fan - Ventilador [package=THT]
  Q5 = NPN-Transistor [package="TO92 [THT]"]
  J12 = female pin header, 2 pins [form="♀ (female)"]
  J13 = female pin header, 2 pins [form="♀ (female)"]
  R40 = Resistor [tolerance=±5% resistance=330 package="2512 [SMD]"]
  J11 = female pin header, 2 pins [form="♀ (female)"]
  J14 = male pin header, 2 pins [form="♂ (male)"]
  J15 = male pin header, 2 pins [form="♂ (male)"]
  J16 = male pin header, 2 pins [form="♂ (male)"]
  J17 = male pin header, 2 pins [form="♂ (male)"]
  J18 = male pin header, 5 pins [form="♂ (male)"]
  J19 = male pin header, 2 pins [form="♂ (male)"]
  J20 = male pin header, 1 pin [form="♂ (male)"]
  J21 = male pin header, 1 pin [form="♂ (male)"]
  J22 = male pin header, 1 pin [form="♂ (male)"]
  J23 = female pin header, 3 pins [form="♀ (female)"]
  C2 = Ceramic Capacitor [capacitance=100nF package="100 mil [THT, multilayer]"]

nets:
  N1: proto2.connectorA7, proto2.connectorX7
  N2: proto2.connectorA9, proto2.connectorW9
  N3: proto2.connectorB2, proto2.connectorB3
  N4: proto2.connectorB12, proto2.connectorB13
  N5: proto2.connectorD4, proto2.connectorD5
  N6: proto2.connectorD10, proto2.connectorD11
  N7: proto2.connectorD14, proto2.connectorD15
  N8: proto2.connectorE1, proto2.connectorW1
  N9: proto2.connectorF1, proto2.connectorY1
  N10: proto2.connectorG4, proto2.connectorG5
  N11: proto2.connectorG10, proto2.connectorG11
  N12: proto2.connectorG14, proto2.connectorG15
  N13: proto2.connectorI2, proto2.connectorI3
  N14: proto2.connectorI9, proto2.connectorY9
  N15: proto2.connectorI12, proto2.connectorI13
  N16: proto2.connectorJ7, proto2.connectorY7
  N17: proto2.connectorW12, Part6.N$60#366, J9.pin2, J17.pin2
  N18: proto2.connectorW14, proto2.connectorY14
  N19: proto2.connectorX12, Part6.N$59#361, J9.pin1, J17.pin1
  N20: proto2.connectorX14, proto2.connectorZ14
  N21: Part6.TXD, Part6.N$53#331
  N22: Part6.RXD, Part6.N$54#336
  N23: Part6.GPIO5, Part6.N$50#316
  N24: Part6.3.3V, Part6.N$51#321, C2.0
  N25: Part6.GND, Part6.N$3#166, Part6.N$11#206, Part6.N$47#301, Part6.N$62#376, R33.Pin_0, C2.1
  N26: Part6.5.0V, Part6.N$1#156, Part6.N$4#171, Part6.N$45#295
  N27: Part6.N$1#159, LED22.anode, J11.pin1, J18.pin1
  N28: Part6.N$2#164, LED22.cathode, J11.pin2, J18.pin2
  N29: Part6.N$2#165, R31.Pin_0
  N30: Part6.N$3#169, J7.gnd, J18.pin3, J23.pin1
  N31: Part6.N$4#174, J7.vcc, J18.pin4, J23.pin2
  N32: Part6.N$4#175, Part6.N$60#370
  N33: Part6.N$5#177, J19.pin1
  N34: Part6.N$5#179, J7.pulse, J18.pin5, J23.pin3
  N35: Part6.N$5#180, U1.pin8
  N36: Part6.N$6#182, J19.pin2
  N37: Part6.N$6#185, U1.pin9
  N38: Part6.N$7, U1.pin11
  N39: Part6.N$8#194, Part6.N$49#315
  N40: Part6.N$8#195, U1.pin10
  N41: Part6.N$9, U1.pin12
  N42: Part6.N$10, U1.pin13
  N43: Part6.N$11#207, J20.pin1
  N44: Part6.N$11#210, U1.pin14
  N45: Part6.N$45#292, F1.5V, J13.pin2, J16.pin2
  N46: Part6.N$46#297, F1.GND, J13.pin1, J16.pin1
  N47: Part6.N$46#299, Q5.E
  N48: Part6.N$47#304, Q5.B
  N49: Part6.N$48#306, R40.Pin_1
  N50: Part6.N$48#309, Q5.C
  N51: Part6.N$49#313, R33.Pin_1
  N52: Part6.N$49#314, R27.P$1, J12.pin2, J15.pin2
  N53: Part6.N$50#320, R40.Pin_0
  N54: Part6.N$51#323, Part6.N$52#328, J14.pin1, J14.pin2
  N55: Part6.N$51#324, R27.P$2, J12.pin1, J15.pin1
  N56: Part6.N$52#330, U1.pin1
  N57: Part6.N$53#335, U1.pin3
  N58: Part6.N$54#340, U1.pin2
  N59: Part6.N$55#343, J22.pin1
  N60: Part6.N$55#344, U1.pin4
  N61: Part6.N$56, U1.pin5
  N62: Part6.N$57#354, R30.Pin_1
  N63: Part6.N$57#355, U1.pin6
  N64: Part6.N$58#358, J21.pin1
  N65: Part6.N$58#360, U1.pin7
  N66: Part6.N$59#363, Q4.E
  N67: Part6.N$59#365, R31.Pin_1
  N68: Part6.N$61#373, Q4.B
  N69: Part6.N$61#374, R30.Pin_0
  N70: Part6.N$62#378, Q4.C

notes:
  Status LED to mimic IR LED brightness
  Front IR LED panel
  Servo to control the camera
  Front photoresistor
  ATTiny84 is powered with a jumper to the 3v line.

custom parts:
  Adafruit Perma-Proto HAT: To kick off the Adafruit HAT party, we have this Perma-Proto inspired plug in daughter board. It has a grid of 0.1" prototyping soldering holes for attaching chips, resistors, LED, potentiometers and more. The holes are connected underneath with traces to mimic the solderless breadboards you're familiar. There's also long power strips for +3V, +5V and Ground connections to the Pi. Near the top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
  ATTiny84: Atmel ATTiny84 processor. 8 ADC pins, 4 PWM pins. Available in either 10MHz or 20MHz. The last 2 pin numbers refer to arduino. D6 = Arduino 6, A6 = Arduino A6 example: PA6 (SDA/MOSI/OC1A/DI/AD6/PCINT6/D6/A6) NOTE: This part is diagrammed to suit the MIT HLT ATTiny84 core at https://github.com/damellis/attiny/
  Fan - Ventilador: Ventilador de 2 pines, se encuentra comunmente en computadoras de escritorio
